# Fritzing sketch hype (saved by Fritzing 0.9.3b)
breadboards: 1

parts:
  Same_board = Arduino Uno (Rev3)
  V1 = DC Power [voltage=16V]
  C1 = Ceramic Capacitor [capacitance=33µF package="100 mil [THT, multilayer]"]
  7812_12V_Regulator = Voltage Regulator [package=to-220-alt]
  C2 = Ceramic Capacitor [capacitance=33µF package="100 mil [THT, multilayer]"]
  IR_Proximity = Infrared Proximity Sensor
  Relay = RELAY [package=relay-jzc]

nets:
  N1: Same_board.A1, IR_Proximity.Vout
  GND: Same_board.GND, V1.V-, C1.0, 7812_12V_Regulator.GND, C2.0, IR_Proximity.GND, Relay.COIL2
  N2: Same_board.D1/TX, Relay.COIL1
  5V: Same_board.5V, IR_Proximity.Vcc
  N3: V1.V+, C1.1, 7812_12V_Regulator.IN
  N4: 7812_12V_Regulator.OUT, C2.1, Relay.MAIN
