# Fritzing sketch hypefive (saved by Fritzing 0.9.3b)
breadboards: 1

parts:
  Same_board = Arduino Uno (Rev3)
  part = DC Power [voltage=16V]
  C1 = Ceramic Capacitor [capacitance=330µF package="100 mil [THT, multilayer]"]
  7806_6V_Regulator = Voltage Regulator [package=to-220-alt]
  C2 = Ceramic Capacitor [capacitance=10µF package="100 mil [THT, multilayer]"]
  IR_Proximity = Infrared Proximity Sensor
  R1 = Resistor [tolerance=±5% resistance=10k package="0805 [SMD]"]
  part_2 = Basic Force Sensing Resistor (FSR) [package=THT]
  part_3 = Basic Servo

nets:
  N1: Same_board.A1, IR_Proximity.Vout
  N2: Same_board.D13/SCK, R1.Pin_0, part_2.pin_1
  N3: Same_board.D5_PWM, part_3.pulse
  5V: Same_board.5V, IR_Proximity.Vcc, part_2.pin_0
  GND: Same_board.GND, part.V-, C1.0, 7806_6V_Regulator.GND, C2.0, IR_Proximity.GND, R1.Pin_1, part_3.gnd
  N4: part.V+, C1.1, 7806_6V_Regulator.IN
  N5: 7806_6V_Regulator.OUT, C2.1, part_3.vcc

notes:
  Force Sensitive Resistor
