# Fritzing sketch shooty (saved by Fritzing 0.9.3b)
breadboards: 1

parts:
  Same_board = Arduino Uno (Rev3)
  part = DC Power [voltage=16V]
  C1 = Ceramic Capacitor [capacitance=330µF package="100 mil [THT, multilayer]"]
  7812_12V_Regulator = Voltage Regulator [package=to-220-alt]
  C2 = Ceramic Capacitor [capacitance=10µF package="100 mil [THT, multilayer]"]
  Relay = RELAY [package=relay-jzc]
  Solenoid = Solenoid
  Light_Dependent_Resistor = Photocell (LDR) [package=THT]
  R1 = Resistor [tolerance=±5% resistance=10k package="0805 [SMD]"]

nets:
  N1: Same_board.D13/SCK, Light_Dependent_Resistor.pin_1, R1.Pin_0
  N2: Same_board.D1/TX, Relay.COIL1
  N3: Same_board.5V, Light_Dependent_Resistor.pin_0
  GND: Same_board.GND, part.V-, C1.0, 7812_12V_Regulator.GND, C2.0, Relay.COIL2, Solenoid.pin2, R1.Pin_1
  N4: part.V+, C1.1, 7812_12V_Regulator.IN
  N5: 7812_12V_Regulator.OUT, C2.1, Relay.MAIN
  N6: Relay.NO, Solenoid.pin1
